// Logisim project 1-bit Full-Adder.circ as structural Verilog: 1 circuit, main circuit main
module main (
  input  A,
  input  B,
  input  Carry,
  output Carry_AB_BC_AC,
  output Sum
);

  wire and_1_out, and_2_out, and_3_out;

  and and_1 (and_1_out, A, B);
  and and_2 (and_2_out, B, Carry);
  and and_3 (and_3_out, A, Carry);
  or or_1 (Carry_AB_BC_AC, and_1_out, and_2_out, and_3_out);
  ExactlyOne xor_1 (.out(Sum), .in0(Carry), .in2(B), .in4(A));
endmodule
