// Logisim project 2-bit Comparator.circ as structural Verilog: 1 circuit, main circuit main
module main (
  input  Y,
  input  in_2,
  input  in_3,
  input  X,
  output X_Y,
  output X_Y_2,
  output out_7
);

  wire and_1_out, and_2_out, and_3_out, and_4_out, and_5_out, and_7_out, not_1_out, not_2_out, not_3_out,
       not_4_out, not_5_out, not_6_out, or_1_out, or_2_out;

  not not_1 (not_1_out, in_2);
  not not_2 (not_2_out, X);
  not not_3 (not_3_out, Y);
  not not_4 (not_4_out, in_3);
  and and_1 (and_1_out, not_1_out, X);
  and and_2 (and_2_out, in_2, not_2_out);
  and and_3 (and_3_out, not_3_out, in_3);
  and and_4 (and_4_out, Y, not_4_out);
  or or_1 (or_1_out, and_1_out, and_2_out);
  or or_2 (or_2_out, and_3_out, and_4_out);
  not not_5 (not_5_out, or_1_out);
  not not_6 (not_6_out, or_2_out);
  and and_5 (and_5_out, and_1_out, not_6_out);
  and and_6 (X_Y_2, not_5_out, not_5_out, not_6_out);
  and and_7 (and_7_out, not_6_out, and_2_out);
  or or_3 (X_Y, and_5_out, and_3_out);
  or or_4 (out_7, and_7_out, and_4_out);

  // Notes on the sheet:
  //   X<Y
endmodule
