// Logisim project 8-bit inverter.circ as structural Verilog: 1 circuit, main circuit main
module main (
  input  A8,
  input  A7,
  input  A6,
  input  A5,
  input  A3,
  input  A2,
  input  A1,
  input  A0,
  input  Inverter,
  output out_10,
  output out_11,
  output out_12,
  output out_13,
  output out_14,
  output out_15,
  output out_16,
  output out_17
);

  xor xor_1 (out_10, A8, Inverter);
  xor xor_2 (out_11, A7, Inverter);
  xor xor_3 (out_12, A6, Inverter);
  xor xor_4 (out_14, A3, Inverter);
  xor xor_5 (out_13, A5, Inverter);
  xor xor_6 (out_15, A2, Inverter);
  xor xor_7 (out_16, A1, Inverter);
  xor xor_8 (out_17, A0, Inverter);
endmodule
