// Logisim project Half-adder.circ as structural Verilog: 1 circuit, main circuit main
module main (
  input  A,
  input  B,
  output Carry_A_B,
  output Sum_XOR_A_B
);

  and and_1 (Carry_A_B, A, B);
  xor xor_1 (Sum_XOR_A_B, A, B);

  // Notes on the sheet:
  //   HALF-ADDER
endmodule
